// Logisim project CPU设计实验1.circ as structural Verilog: 11 circuits, main circuit main
module main (
  input  in_1
);

  wire alusrc, clk, extop, isbeq, memtoreg, memwrite, regdst, regwrite, zero;
  wire [1:0] aluop;
  wire [4:0] multiplexer_1_out, rs, rt;
  wire [5:0] opcode;
  wire [15:0] addr_imm;
  wire [31:0] ALU_out_4, \ext_1__32位输出 , gpr_1_rd1, gpr_1_rd2, multiplexer_2_out, multiplexer_3_out,
       ram_1_data;

  Clock #(.highDuration(1), .lowDuration(1)) clock_1 (.out(clk));
  IFU ifu_1 (.CLK(clk), .IFBEQ(isbeq), .ZERO(zero), .RESET(in_1), .\输出指令 ({opcode, rs, rt, addr_imm}));
  CONTROLLER controller_1 (
    .FUNC(addr_imm[5:0]), .OPCODE(opcode), .RegDst(regdst), .ALUSrc(alusrc), .MemtoReg(memtoreg),
    .RegWrite(regwrite), .MemWrite(memwrite), .ALUOp_1_0(aluop), .ExtOp(extop), .ISBEQ(isbeq));
  Multiplexer #(.select(1), .width(5), .disabled("Z"), .enable("false")) multiplexer_1 (
    .in0(rt), .in1(addr_imm[15:11]), .out(multiplexer_1_out), .sel(regdst));
  GPR gpr_1 (
    .WD(multiplexer_3_out), .regwrite(clk), .clk(regwrite), .a1(rs), .a2(rt), .a3(multiplexer_1_out),
    .rd1(gpr_1_rd1), .rd2(gpr_1_rd2));  // open: reset
  EXT ext_1 (._16bit_input(addr_imm), .ExtOp(extop), .\_32位输出 (\ext_1__32位输出 ));
  Multiplexer #(.select(1), .width(32), .disabled("Z"), .enable("false")) multiplexer_2 (
    .in0(gpr_1_rd2), .in1(\ext_1__32位输出 ), .out(multiplexer_2_out), .sel(alusrc));
  ALU ALU (.INPUT1(gpr_1_rd1), .ALUop(aluop), .INPUT2(multiplexer_2_out), .out_4(ALU_out_4), .zero(zero));
  Multiplexer #(.select(1), .width(32), .disabled("Z"), .enable("false")) multiplexer_3 (
    .in0(ALU_out_4), .in1(ram_1_data), .out(multiplexer_3_out), .sel(memtoreg));
  // Probe on zero
  RAM #(.addrWidth(5), .dataWidth(32), .bus("separate"), .Select("high")) ram_1 (
    .addr(ALU_out_4[4:0]), .din(gpr_1_rd2), .data(ram_1_data), .str(memwrite), .clk(clk), .clr(in_1));  // open: sel, ld

  // Other names for the same wires on the sheet: func[5:0] = addr_imm[5:0]; rd[4:0] = addr_imm[15:11]; reset = in_1;
  //   shamt[4:0] = addr_imm[10:6]
endmodule

module \一位全加器  (
  input  input1,
  input  input2,
  input  carryin,
  output \output ,
  output carryout
);

  wire and_1_out, and_2_out, and_3_out, and_4_out, and_5_out, and_6_out, and_7_out, not_1_out, not_2_out,
       not_3_out, not_4_out, not_5_out, not_6_out;

  not not_1 (not_1_out, input1);
  not not_2 (not_2_out, input2);
  not not_3 (not_3_out, input1);
  not not_4 (not_4_out, carryin);
  not not_5 (not_5_out, input2);
  not not_6 (not_6_out, carryin);
  and and_1 (and_1_out, input2, carryin);
  and and_2 (and_2_out, input1, carryin);
  and and_3 (and_3_out, input1, input2);
  and and_4 (and_4_out, not_1_out, not_2_out, carryin);
  and and_5 (and_5_out, not_3_out, input2, not_4_out);
  and and_6 (and_6_out, input1, not_5_out, not_6_out);
  and and_7 (and_7_out, input1, input2, carryin);
  or or_1 (carryout, and_1_out, and_2_out, and_3_out);
  or or_2 (\output , and_4_out, and_5_out, and_6_out, and_7_out);

  // Notes on the sheet:
  //   input2: pull=down
  //   carryin: pull=down
  //   input1: pull=down
  //                  输入：input1，input2   低位进位 carryin
  //                     输出output  向高位进位carrryout
  //   一位全加器
endmodule

module \_32位加法器  (
  input  [31:0] INPUT_X,
  input  [31:0] INPUT_Y,
  output [31:0] OUTPUT
);

  wire C31, C32, \一位全加器_1_carryout , \一位全加器_2_carryout , \一位全加器_3_carryout , \一位全加器_4_carryout ,
       \一位全加器_5_carryout , \一位全加器_6_carryout , \一位全加器_7_carryout , \一位全加器_8_carryout , \一位全加器_9_carryout ,
       \一位全加器_10_carryout , \一位全加器_11_carryout , \一位全加器_12_carryout , \一位全加器_13_carryout ,
       \一位全加器_14_carryout , \一位全加器_15_carryout , \一位全加器_16_carryout , \一位全加器_17_carryout ,
       \一位全加器_18_carryout , \一位全加器_19_carryout , \一位全加器_20_carryout , \一位全加器_21_carryout ,
       \一位全加器_22_carryout , \一位全加器_23_carryout , \一位全加器_24_carryout , \一位全加器_25_carryout ,
       \一位全加器_26_carryout , \一位全加器_27_carryout , \一位全加器_28_carryout , \一位全加器_29_carryout ,
       \一位全加器_30_carryout ;

  \一位全加器  \u_一位全加器_1  (
    .input1(INPUT_X[0]), .input2(INPUT_Y[0]), .carryin(1'b0), .\output (OUTPUT[0]),
    .carryout(\一位全加器_1_carryout ));
  \一位全加器  \u_一位全加器_2  (
    .input1(INPUT_X[1]), .input2(INPUT_Y[1]), .carryin(\一位全加器_1_carryout ), .\output (OUTPUT[1]),
    .carryout(\一位全加器_2_carryout ));
  \一位全加器  \u_一位全加器_3  (
    .input1(INPUT_X[2]), .input2(INPUT_Y[2]), .carryin(\一位全加器_2_carryout ), .\output (OUTPUT[2]),
    .carryout(\一位全加器_3_carryout ));
  \一位全加器  \u_一位全加器_4  (
    .input1(INPUT_X[3]), .input2(INPUT_Y[3]), .carryin(\一位全加器_3_carryout ), .\output (OUTPUT[3]),
    .carryout(\一位全加器_4_carryout ));
  \一位全加器  \u_一位全加器_5  (
    .input1(INPUT_X[4]), .input2(INPUT_Y[4]), .carryin(\一位全加器_4_carryout ), .\output (OUTPUT[4]),
    .carryout(\一位全加器_5_carryout ));
  \一位全加器  \u_一位全加器_6  (
    .input1(INPUT_X[6]), .input2(INPUT_Y[6]), .carryin(\一位全加器_7_carryout ), .\output (OUTPUT[6]),
    .carryout(\一位全加器_6_carryout ));
  \一位全加器  \u_一位全加器_7  (
    .input1(INPUT_X[5]), .input2(INPUT_Y[5]), .carryin(\一位全加器_5_carryout ), .\output (OUTPUT[5]),
    .carryout(\一位全加器_7_carryout ));
  \一位全加器  \u_一位全加器_8  (
    .input1(INPUT_X[7]), .input2(INPUT_Y[7]), .carryin(\一位全加器_6_carryout ), .\output (OUTPUT[7]),
    .carryout(\一位全加器_8_carryout ));
  \一位全加器  \u_一位全加器_9  (
    .input1(INPUT_X[8]), .input2(INPUT_Y[8]), .carryin(\一位全加器_8_carryout ), .\output (OUTPUT[8]),
    .carryout(\一位全加器_9_carryout ));
  \一位全加器  \u_一位全加器_10  (
    .input1(INPUT_X[10]), .input2(INPUT_Y[10]), .carryin(\一位全加器_11_carryout ), .\output (OUTPUT[10]),
    .carryout(\一位全加器_10_carryout ));
  \一位全加器  \u_一位全加器_11  (
    .input1(INPUT_X[9]), .input2(INPUT_Y[9]), .carryin(\一位全加器_9_carryout ), .\output (OUTPUT[9]),
    .carryout(\一位全加器_11_carryout ));
  \一位全加器  \u_一位全加器_12  (
    .input1(INPUT_X[11]), .input2(INPUT_Y[11]), .carryin(\一位全加器_10_carryout ), .\output (OUTPUT[11]),
    .carryout(\一位全加器_12_carryout ));
  \一位全加器  \u_一位全加器_13  (
    .input1(INPUT_X[12]), .input2(INPUT_Y[12]), .carryin(\一位全加器_12_carryout ), .\output (OUTPUT[12]),
    .carryout(\一位全加器_13_carryout ));
  \一位全加器  \u_一位全加器_14  (
    .input1(INPUT_X[14]), .input2(INPUT_Y[14]), .carryin(\一位全加器_15_carryout ), .\output (OUTPUT[14]),
    .carryout(\一位全加器_14_carryout ));
  \一位全加器  \u_一位全加器_15  (
    .input1(INPUT_X[13]), .input2(INPUT_Y[13]), .carryin(\一位全加器_13_carryout ), .\output (OUTPUT[13]),
    .carryout(\一位全加器_15_carryout ));
  \一位全加器  \u_一位全加器_16  (
    .input1(INPUT_X[15]), .input2(INPUT_Y[15]), .carryin(\一位全加器_14_carryout ), .\output (OUTPUT[15]),
    .carryout(\一位全加器_16_carryout ));
  \一位全加器  \u_一位全加器_17  (
    .input1(INPUT_X[16]), .input2(INPUT_Y[16]), .carryin(\一位全加器_16_carryout ), .\output (OUTPUT[16]),
    .carryout(\一位全加器_17_carryout ));
  \一位全加器  \u_一位全加器_18  (
    .input1(INPUT_X[18]), .input2(INPUT_Y[18]), .carryin(\一位全加器_19_carryout ), .\output (OUTPUT[18]),
    .carryout(\一位全加器_18_carryout ));
  \一位全加器  \u_一位全加器_19  (
    .input1(INPUT_X[17]), .input2(INPUT_Y[17]), .carryin(\一位全加器_17_carryout ), .\output (OUTPUT[17]),
    .carryout(\一位全加器_19_carryout ));
  \一位全加器  \u_一位全加器_20  (
    .input1(INPUT_X[19]), .input2(INPUT_Y[19]), .carryin(\一位全加器_18_carryout ), .\output (OUTPUT[19]),
    .carryout(\一位全加器_20_carryout ));
  \一位全加器  \u_一位全加器_21  (
    .input1(INPUT_X[20]), .input2(INPUT_Y[20]), .carryin(\一位全加器_20_carryout ), .\output (OUTPUT[20]),
    .carryout(\一位全加器_21_carryout ));
  \一位全加器  \u_一位全加器_22  (
    .input1(INPUT_X[22]), .input2(INPUT_Y[22]), .carryin(\一位全加器_23_carryout ), .\output (OUTPUT[22]),
    .carryout(\一位全加器_22_carryout ));
  \一位全加器  \u_一位全加器_23  (
    .input1(INPUT_X[21]), .input2(INPUT_Y[21]), .carryin(\一位全加器_21_carryout ), .\output (OUTPUT[21]),
    .carryout(\一位全加器_23_carryout ));
  \一位全加器  \u_一位全加器_24  (
    .input1(INPUT_X[23]), .input2(INPUT_Y[23]), .carryin(\一位全加器_22_carryout ), .\output (OUTPUT[23]),
    .carryout(\一位全加器_24_carryout ));
  \一位全加器  \u_一位全加器_25  (
    .input1(INPUT_X[24]), .input2(INPUT_Y[24]), .carryin(\一位全加器_24_carryout ), .\output (OUTPUT[24]),
    .carryout(\一位全加器_25_carryout ));
  \一位全加器  \u_一位全加器_26  (
    .input1(INPUT_X[26]), .input2(INPUT_Y[26]), .carryin(\一位全加器_27_carryout ), .\output (OUTPUT[26]),
    .carryout(\一位全加器_26_carryout ));
  \一位全加器  \u_一位全加器_27  (
    .input1(INPUT_X[25]), .input2(INPUT_Y[25]), .carryin(\一位全加器_25_carryout ), .\output (OUTPUT[25]),
    .carryout(\一位全加器_27_carryout ));
  \一位全加器  \u_一位全加器_28  (
    .input1(INPUT_X[27]), .input2(INPUT_Y[27]), .carryin(\一位全加器_26_carryout ), .\output (OUTPUT[27]),
    .carryout(\一位全加器_28_carryout ));
  \一位全加器  \u_一位全加器_29  (
    .input1(INPUT_X[28]), .input2(INPUT_Y[28]), .carryin(\一位全加器_28_carryout ), .\output (OUTPUT[28]),
    .carryout(\一位全加器_29_carryout ));
  \一位全加器  \u_一位全加器_30  (
    .input1(INPUT_X[29]), .input2(INPUT_Y[29]), .carryin(\一位全加器_29_carryout ), .\output (OUTPUT[29]),
    .carryout(\一位全加器_30_carryout ));
  \一位全加器  \u_一位全加器_31  (
    .input1(INPUT_X[30]), .input2(INPUT_Y[30]), .carryin(\一位全加器_30_carryout ), .\output (OUTPUT[30]),
    .carryout(C31));
  \一位全加器  \u_一位全加器_32  (
    .input1(INPUT_X[31]), .input2(INPUT_Y[31]), .carryin(C31), .\output (OUTPUT[31]), .carryout(C32));

  // Other names for the same wires on the sheet: X0 = INPUT_X[0]; X1 = INPUT_X[1]; X2 = INPUT_X[2]; X3 = INPUT_X[3];
  //   X4 = INPUT_X[4]; X5 = INPUT_X[5]; X6 = INPUT_X[6]; X7 = INPUT_X[7]; X8 = INPUT_X[8]; X9 = INPUT_X[9];
  //   X10 = INPUT_X[10]; X11 = INPUT_X[11]; X12 = INPUT_X[12]; X13 = INPUT_X[13]; X14 = INPUT_X[14];
  //   X15 = INPUT_X[15]; X16 = INPUT_X[16]; X17 = INPUT_X[17]; X18 = INPUT_X[18]; X19 = INPUT_X[19];
  //   X20 = INPUT_X[20]; X21 = INPUT_X[21]; X22 = INPUT_X[22]; X23 = INPUT_X[23]; X24 = INPUT_X[24];
  //   X25 = INPUT_X[25]; X26 = INPUT_X[26]; X27 = INPUT_X[27]; X28 = INPUT_X[28]; X29 = INPUT_X[29];
  //   X30 = INPUT_X[30]; X31 = INPUT_X[31]; Y0 = INPUT_Y[0]; Y1 = INPUT_Y[1]; Y2 = INPUT_Y[2]; Y3 = INPUT_Y[3];
  //   Y4 = INPUT_Y[4]; Y5 = INPUT_Y[5]; Y6 = INPUT_Y[6]; Y7 = INPUT_Y[7]; Y8 = INPUT_Y[8]; Y9 = INPUT_Y[9];
  //   Y10 = INPUT_Y[10]; Y11 = INPUT_Y[11]; Y12 = INPUT_Y[12]; Y13 = INPUT_Y[13]; Y14 = INPUT_Y[14];
  //   Y15 = INPUT_Y[15]; Y16 = INPUT_Y[16]; Y17 = INPUT_Y[17]; Y18 = INPUT_Y[18]; Y19 = INPUT_Y[19];
  //   Y20 = INPUT_Y[20]; Y21 = INPUT_Y[21]; Y22 = INPUT_Y[22]; Y23 = INPUT_Y[23]; Y24 = INPUT_Y[24];
  //   Y25 = INPUT_Y[25]; Y26 = INPUT_Y[26]; Y27 = INPUT_Y[27]; Y28 = INPUT_Y[28]; Y29 = INPUT_Y[29];
  //   Y30 = INPUT_Y[30]; Y31 = INPUT_Y[31]; Z0 = OUTPUT[0]; Z1 = OUTPUT[1]; Z2 = OUTPUT[2]; Z3 = OUTPUT[3];
  //   Z4 = OUTPUT[4]; Z5 = OUTPUT[5]; Z6 = OUTPUT[6]; Z7 = OUTPUT[7]; Z8 = OUTPUT[8]; Z9 = OUTPUT[9];
  //   Z10 = OUTPUT[10]; Z11 = OUTPUT[11]; Z12 = OUTPUT[12]; Z13 = OUTPUT[13]; Z14 = OUTPUT[14]; Z15 = OUTPUT[15];
  //   Z16 = OUTPUT[16]; Z17 = OUTPUT[17]; Z18 = OUTPUT[18]; Z19 = OUTPUT[19]; Z20 = OUTPUT[20]; Z21 = OUTPUT[21];
  //   Z22 = OUTPUT[22]; Z23 = OUTPUT[23]; Z24 = OUTPUT[24]; Z25 = OUTPUT[25]; Z26 = OUTPUT[26]; Z27 = OUTPUT[27];
  //   Z28 = OUTPUT[28]; Z29 = OUTPUT[29]; Z30 = OUTPUT[30]; Z31 = OUTPUT[31]

  // Notes on the sheet:
  //   32BIT ADDER
endmodule

module \_32位减法器  (
  input  [31:0] INTPUT1,
  input  [31:0] INPUT2,
  output [31:0] OUTPUT
);

  wire [31:0] \n32位加法器_1_output , not_1_out;

  // Probe on not_1_out
  assign not_1_out = ~INPUT2;  // NOT_Gate not_1, 32 bits wide
  \_32位加法器  \u_32位加法器_1  (.INPUT_X(not_1_out), .INPUT_Y(32'h1), .OUTPUT(\n32位加法器_1_output ));
  \_32位加法器  \u_32位加法器_2  (.INPUT_X(INTPUT1), .INPUT_Y(\n32位加法器_1_output ), .OUTPUT(OUTPUT));
endmodule

// OR
module \ORI指令器件  (
  input  [31:0] INPUT,
  input  [31:0] \无符号位拓展后的立即数 ,
  output [31:0] OUTPUT
);

  assign OUTPUT = INPUT | \无符号位拓展后的立即数 ;  // OR_Gate or_1, 32 bits wide
endmodule

module ALU (
  input  [31:0] INPUT1,
  input  [1:0] ALUop,
  input  [31:0] INPUT2,
  output [31:0] out_4,
  output zero
);

  wire [31:0] \_32位减法器_output , \_32位加法器_output , \ori指令器件_1_output ;

  \ORI指令器件  \ori指令器件_1  (.INPUT(INPUT1), .\无符号位拓展后的立即数 (INPUT2), .OUTPUT(\ori指令器件_1_output ));
  \_32位减法器  \_32位减法器  (.INTPUT1(INPUT1), .INPUT2(INPUT2), .OUTPUT(\_32位减法器_output ));
  \_32位加法器  \_32位加法器  (.INPUT_X(INPUT1), .INPUT_Y(INPUT2), .OUTPUT(\_32位加法器_output ));
  Multiplexer #(.select(2), .width(32), .disabled("Z"), .enable("false")) multiplexer_1 (
    .in0({32{1'b0}}), .in1(\ori指令器件_1_output ), .in2(\_32位减法器_output ), .in3(\_32位加法器_output ), .out(out_4),
    .sel(ALUop));
  Comparator #(.width(32), .mode("unsigned")) comparator_1 (.a(out_4), .b({32{1'b0}}), .eq(zero));  // open: gt, lt

  // Notes on the sheet:
  //   out_4: pull=down
  //   zero: pull=down
endmodule

module IFU (
  input  CLK,
  input  IFBEQ,
  input  ZERO,
  input  RESET,
  output [31:0] \输出指令 
);

  wire and_1_out;
  wire [29:0] PC_q;
  wire [31:0] \_32bit加法器_output , bit_extender_1_out, bit_extender_2_out, multiplexer_1_out,
       \n32位加法器_1_output ;

  Register #(.width(30), .trigger("rising"), .Select("low")) PC (
    .D(multiplexer_1_out[29:0]), .Q(PC_q), .clk(CLK), .clr(RESET));  // open: en
  assign bit_extender_1_out = {{2{1'b0}}, PC_q};  // Bit_Extender bit_extender_1
  ROM #(.addrWidth(5), .dataWidth(32), .Select("high")) rom_1 (.addr(PC_q[4:0]), .data(\输出指令 ));
  \_32位加法器  \_32bit加法器  (.INPUT_X(bit_extender_1_out), .INPUT_Y(32'h1), .OUTPUT(\_32bit加法器_output ));
  assign bit_extender_2_out = {{16{1'b0}}, \输出指令 [15:0]};  // Bit_Extender bit_extender_2
  \_32位加法器  \u_32位加法器_1  (.INPUT_X(\_32bit加法器_output ), .INPUT_Y(bit_extender_2_out), .OUTPUT(\n32位加法器_1_output ));
  Multiplexer #(.select(1), .width(32), .disabled("Z"), .enable("false")) multiplexer_1 (
    .in0(\_32bit加法器_output ), .in1(\n32位加法器_1_output ), .out(multiplexer_1_out), .sel(and_1_out));
  and and_1 (and_1_out, IFBEQ, ZERO);
endmodule

module CONTROLLER (
  input  [5:0] FUNC,
  input  [5:0] OPCODE,
  output ExtOp,
  output ISBEQ,
  output RegDst,
  output ALUSrc,
  output MemtoReg,
  output RegWrite,
  output MemWrite,
  output [1:0] ALUOp_1_0
);

  wire ADDU_out, LW_out, not_1_out, not_2_out, not_3_out, not_4_out, not_5_out, not_6_out, not_7_out,
       not_8_out, not_9_out, not_10_out, not_11_out, not_12_out, ORI_out, SUBU_out;

  not not_1 (not_1_out, FUNC[5]);
  not not_2 (not_2_out, FUNC[3]);
  not not_3 (not_3_out, FUNC[4]);
  not not_4 (not_4_out, FUNC[2]);
  not not_5 (not_5_out, FUNC[0]);
  not not_6 (not_6_out, FUNC[1]);
  not not_7 (not_7_out, OPCODE[4]);
  not not_8 (not_8_out, OPCODE[5]);
  not not_9 (not_9_out, OPCODE[3]);
  not not_10 (not_10_out, OPCODE[2]);
  not not_11 (not_11_out, OPCODE[0]);
  not not_12 (not_12_out, OPCODE[1]);
  and ADDU (ADDU_out, FUNC[5], not_3_out, not_2_out, not_4_out, not_6_out, FUNC[0], not_8_out, not_7_out, not_9_out, not_10_out, not_12_out, not_11_out);
  and SUBU (SUBU_out, FUNC[5], not_3_out, not_2_out, not_4_out, FUNC[1], FUNC[0], not_8_out, not_7_out, not_9_out, not_10_out, not_12_out, not_11_out);
  and ORI (ORI_out, not_8_out, not_7_out, OPCODE[3], OPCODE[2], not_12_out, OPCODE[0]);
  and LW (LW_out, OPCODE[5], not_7_out, not_9_out, not_10_out, OPCODE[1], OPCODE[0]);
  and SW (MemWrite, OPCODE[5], not_7_out, OPCODE[3], not_10_out, OPCODE[1], OPCODE[0]);
  and BEQ (ISBEQ, not_8_out, not_7_out, not_9_out, OPCODE[2], not_12_out, not_11_out);
  and LUI (ExtOp, not_8_out, not_7_out, OPCODE[3], OPCODE[2], OPCODE[1], OPCODE[0]);
  or u_RegDst (RegDst, ADDU_out, SUBU_out);
  or u_ALUSrc (ALUSrc, ORI_out, LW_out, MemWrite, ExtOp);
  buf u_MemtoReg (MemtoReg, LW_out);  // OR_Gate
  or u_RegWrite (RegWrite, ADDU_out, SUBU_out, ExtOp, ORI_out, LW_out);
  or ALUOp1 (ALUOp_1_0[1], SUBU_out, ADDU_out);
  or ALUOp0 (ALUOp_1_0[0], ORI_out, ADDU_out);

  // Other names for the same wires on the sheet: F0 = FUNC[0]; F1 = FUNC[1]; F2 = FUNC[2]; F3 = FUNC[3]; F4 = FUNC[4];
  //   F5 = FUNC[5]; OP0 = OPCODE[0]; OP1 = OPCODE[1]; OP2 = OPCODE[2]; OP3 = OPCODE[3]; OP4 = OPCODE[4];
  //   OP5 = OPCODE[5]

  // Notes on the sheet:
  //   0
  //   1
  //   000000addu   000000subu   001101ori   100011lw   101011sw   000100beq   001111lui    000010j
  //   1
  //   0
endmodule

module GPR (
  input  regwrite,
  input  clk,
  input  reset,
  input  [4:0] a1,
  input  [4:0] a2,
  input  [4:0] a3,
  input  [31:0] WD,
  output [31:0] rd1,
  output [31:0] rd2
);

  wire demultiplexer_1_out0, demultiplexer_1_out1, demultiplexer_1_out2, demultiplexer_1_out3,
       demultiplexer_1_out4, demultiplexer_1_out5, demultiplexer_1_out6, demultiplexer_1_out7,
       demultiplexer_1_out8, demultiplexer_1_out9, demultiplexer_1_out10, demultiplexer_1_out11,
       demultiplexer_1_out12, demultiplexer_1_out13, demultiplexer_1_out14, demultiplexer_1_out15,
       demultiplexer_1_out16, demultiplexer_1_out17, demultiplexer_1_out18, demultiplexer_1_out19,
       demultiplexer_1_out20, demultiplexer_1_out21, demultiplexer_1_out22, demultiplexer_1_out23,
       demultiplexer_1_out24, demultiplexer_1_out25, demultiplexer_1_out26, demultiplexer_1_out27,
       demultiplexer_1_out28, demultiplexer_1_out29, demultiplexer_1_out30, demultiplexer_1_out31;
  wire [31:0] _0, _1, _2, _3, _4, _5, _6, _7, _8, _9, _10, _11, _12, _13, _14, _15, _16, _17, _18, _19, _20,
       _21, _22, _23, _24, _25, _26, _27, _28, _29, _30, _31;

  Demultiplexer #(.select(5), .width(1), .tristate("false"), .disabled("Z"), .enable("false")) demultiplexer_1 (
    .out0(demultiplexer_1_out0), .out1(demultiplexer_1_out1), .out2(demultiplexer_1_out2),
    .out3(demultiplexer_1_out3), .out4(demultiplexer_1_out4), .out5(demultiplexer_1_out5),
    .out6(demultiplexer_1_out6), .out7(demultiplexer_1_out7), .out8(demultiplexer_1_out8),
    .out9(demultiplexer_1_out9), .out10(demultiplexer_1_out10), .out11(demultiplexer_1_out11),
    .out12(demultiplexer_1_out12), .out13(demultiplexer_1_out13), .out14(demultiplexer_1_out14),
    .out15(demultiplexer_1_out15), .out16(demultiplexer_1_out16), .out17(demultiplexer_1_out17),
    .out18(demultiplexer_1_out18), .out19(demultiplexer_1_out19), .out20(demultiplexer_1_out20),
    .out21(demultiplexer_1_out21), .out22(demultiplexer_1_out22), .out23(demultiplexer_1_out23),
    .out24(demultiplexer_1_out24), .out25(demultiplexer_1_out25), .out26(demultiplexer_1_out26),
    .out27(demultiplexer_1_out27), .out28(demultiplexer_1_out28), .out29(demultiplexer_1_out29),
    .out30(demultiplexer_1_out30), .out31(demultiplexer_1_out31), .in(regwrite), .sel(a3));
  Register #(.width(32), .trigger("rising"), .Select("low")) register_1 (
    .D(WD), .en(demultiplexer_1_out0), .Q(_0), .clk(clk), .clr(reset));
  Register #(.width(32), .trigger("rising"), .Select("low")) register_2 (
    .D(WD), .en(demultiplexer_1_out1), .Q(_1), .clk(clk), .clr(reset));
  Register #(.width(32), .trigger("rising"), .Select("low")) register_3 (
    .D(WD), .en(demultiplexer_1_out2), .Q(_2), .clk(clk), .clr(reset));
  Register #(.width(32), .trigger("rising"), .Select("low")) register_4 (
    .D(WD), .en(demultiplexer_1_out3), .Q(_3), .clk(clk), .clr(reset));
  Register #(.width(32), .trigger("rising"), .Select("low")) register_5 (
    .D(WD), .en(demultiplexer_1_out4), .Q(_4), .clk(clk), .clr(reset));
  Register #(.width(32), .trigger("rising"), .Select("low")) register_6 (
    .D(WD), .en(demultiplexer_1_out5), .Q(_5), .clk(clk), .clr(reset));
  Register #(.width(32), .trigger("rising"), .Select("low")) register_7 (
    .D(WD), .en(demultiplexer_1_out6), .Q(_6), .clk(clk), .clr(reset));
  Register #(.width(32), .trigger("rising"), .Select("low")) register_8 (
    .D(WD), .en(demultiplexer_1_out7), .Q(_7), .clk(clk), .clr(reset));
  Register #(.width(32), .trigger("rising"), .Select("low")) register_9 (
    .D(WD), .en(demultiplexer_1_out8), .Q(_8), .clk(clk), .clr(reset));
  Register #(.width(32), .trigger("rising"), .Select("low")) register_10 (
    .D(WD), .en(demultiplexer_1_out9), .Q(_9), .clk(clk), .clr(reset));
  Register #(.width(32), .trigger("rising"), .Select("low")) register_11 (
    .D(WD), .en(demultiplexer_1_out10), .Q(_10), .clk(clk), .clr(reset));
  Register #(.width(32), .trigger("rising"), .Select("low")) register_12 (
    .D(WD), .en(demultiplexer_1_out11), .Q(_11), .clk(clk), .clr(reset));
  Register #(.width(32), .trigger("rising"), .Select("low")) register_13 (
    .D(WD), .en(demultiplexer_1_out12), .Q(_12), .clk(clk), .clr(reset));
  Register #(.width(32), .trigger("rising"), .Select("low")) register_14 (
    .D(WD), .en(demultiplexer_1_out13), .Q(_13), .clk(clk), .clr(reset));
  Register #(.width(32), .trigger("rising"), .Select("low")) register_15 (
    .D(WD), .en(demultiplexer_1_out14), .Q(_14), .clk(clk), .clr(reset));
  Register #(.width(32), .trigger("rising"), .Select("low")) register_16 (
    .D(WD), .en(demultiplexer_1_out15), .Q(_15), .clk(clk), .clr(reset));
  Register #(.width(32), .trigger("rising"), .Select("low")) register_17 (
    .D(WD), .en(demultiplexer_1_out16), .Q(_16), .clk(clk), .clr(reset));
  Register #(.width(32), .trigger("rising"), .Select("low")) register_18 (
    .D(WD), .en(demultiplexer_1_out17), .Q(_17), .clk(clk), .clr(reset));
  Register #(.width(32), .trigger("rising"), .Select("low")) register_19 (
    .D(WD), .en(demultiplexer_1_out18), .Q(_18), .clk(clk), .clr(reset));
  Register #(.width(32), .trigger("rising"), .Select("low")) register_20 (
    .D(WD), .en(demultiplexer_1_out19), .Q(_19), .clk(clk), .clr(reset));
  Register #(.width(32), .trigger("rising"), .Select("low")) register_21 (
    .D(WD), .en(demultiplexer_1_out20), .Q(_20), .clk(clk), .clr(reset));
  Register #(.width(32), .trigger("rising"), .Select("low")) register_22 (
    .D(WD), .en(demultiplexer_1_out21), .Q(_21), .clk(clk), .clr(reset));
  Register #(.width(32), .trigger("rising"), .Select("low")) register_23 (
    .D(WD), .en(demultiplexer_1_out22), .Q(_22), .clk(clk), .clr(reset));
  Register #(.width(32), .trigger("rising"), .Select("low")) register_24 (
    .D(WD), .en(demultiplexer_1_out23), .Q(_23), .clk(clk), .clr(reset));
  Register #(.width(32), .trigger("rising"), .Select("low")) register_25 (
    .D(WD), .en(demultiplexer_1_out24), .Q(_24), .clk(clk), .clr(reset));
  Register #(.width(32), .trigger("rising"), .Select("low")) register_26 (
    .D(WD), .en(demultiplexer_1_out25), .Q(_25), .clk(clk), .clr(reset));
  Register #(.width(32), .trigger("rising"), .Select("low")) register_27 (
    .D(WD), .en(demultiplexer_1_out26), .Q(_26), .clk(clk), .clr(reset));
  Register #(.width(32), .trigger("rising"), .Select("low")) register_28 (
    .D(WD), .en(demultiplexer_1_out27), .Q(_27), .clk(clk), .clr(reset));
  Register #(.width(32), .trigger("rising"), .Select("low")) register_29 (
    .D(WD), .en(demultiplexer_1_out28), .Q(_28), .clk(clk), .clr(reset));
  Register #(.width(32), .trigger("rising"), .Select("low")) register_30 (
    .D(WD), .en(demultiplexer_1_out29), .Q(_29), .clk(clk), .clr(reset));
  Register #(.width(32), .trigger("rising"), .Select("low")) register_31 (
    .D(WD), .en(demultiplexer_1_out30), .Q(_30), .clk(clk), .clr(reset));
  Register #(.width(32), .trigger("rising"), .Select("low")) register_32 (
    .D(WD), .en(demultiplexer_1_out31), .Q(_31), .clk(clk), .clr(reset));
  Multiplexer #(.select(5), .width(32), .disabled("Z"), .enable("false")) multiplexer_1 (
    .in0(_0), .in1(_1), .in2(_2), .in3(_3), .in4(_4), .in5(_5), .in6(_6), .in7(_7), .in8(_8), .in9(_9),
    .in10(_10), .in11(_11), .in12(_12), .in13(_13), .in14(_14), .in15(_15), .in16(_16), .in17(_17),
    .in18(_18), .in19(_19), .in20(_20), .in21(_21), .in22(_22), .in23(_23), .in24(_24), .in25(_25),
    .in26(_26), .in27(_27), .in28(_28), .in29(_29), .in30(_30), .in31(_31), .out(rd1), .sel(a1));
  Multiplexer #(.select(5), .width(32), .disabled("Z"), .enable("false")) multiplexer_2 (
    .in0(_0), .in1(_1), .in2(_2), .in3(_3), .in4(_4), .in5(_5), .in6(_6), .in7(_7), .in8(_8), .in9(_9),
    .in10(_10), .in11(_11), .in12(_12), .in13(_13), .in14(_14), .in15(_15), .in16(_16), .in17(_17),
    .in18(_18), .in19(_19), .in20(_20), .in21(_21), .in22(_22), .in23(_23), .in24(_24), .in25(_25),
    .in26(_26), .in27(_27), .in28(_28), .in29(_29), .in30(_30), .in31(_31), .out(rd2), .sel(a2));

  // Notes on the sheet:
  //   reset: pull=down
  //   $v1
  //   $t0
  //   $zero
  //   $at
  //   $v0
  //   $a0
  //   $a1
  //   $a2
  //   $a3
  //   $t1
  //   $t2
  //   $t3
  //   $t4
  //   $t5
  //   $t6
  //   $t7
  //   $s0
  //   $s1
  //   $s2
  //   $s3
  //   $s4
  //   $s5
  //   $s6
  //   $s7
  //   $t8
  //   $t9
  //   $k0
  //   $k1
  //   $gp
  //   $sp
  //   $fp
  //   $ra
endmodule

module EXT (
  input  [15:0] _16bit_input,
  input  ExtOp,
  output [31:0] \_32位输出 
);

  wire [31:0] bit_extender_1_out;

  assign bit_extender_1_out = {{16{1'b0}}, _16bit_input};  // Bit_Extender bit_extender_1
  Multiplexer #(.select(1), .width(32), .disabled("Z"), .enable("false")) multiplexer_1 (
    .in0(bit_extender_1_out), .in1({_16bit_input, {16{1'b0}}}), .out(\_32位输出 ), .sel(ExtOp));
endmodule

module TEST (
  input  [1:0] in_1,
  input  [31:0] in_2,
  input  [31:0] in_3,
  output [31:0] out_4,
  output out_5
);

  ALU alu_1 (.INPUT1(in_2), .ALUop(in_1), .INPUT2(in_3), .out_4(out_4), .zero(out_5));

  // Notes on the sheet:
  //   out_5: pull=down
  //   out_4: pull=down
endmodule
